// Logisim project Lab 7.circ as structural Verilog: 1 circuit, main circuit main
module main (
  input  L,
  input  R,
  input  H,
  output out_4,
  output out_5,
  output out_6,
  output out_7,
  output out_8,
  output out_9
);

  wire and_1_out, and_2_out, and_3_out, and_4_out, and_5_out, and_6_out, and_7_out, and_8_out, and_9_out,
       and_10_out, and_11_out, and_12_out, and_13_out, and_14_out, and_16_out, and_17_out, and_18_out,
       clock_1_out, d_ff_1_qn, d_ff_2_q, d_ff_2_qn, d_ff_3_q, d_ff_3_qn, not_1_out, or_1_out, or_2_out,
       or_3_out, or_4_out, xor_1_out;

  Clock clock_1 (.out(clock_1_out));
  not not_1 (not_1_out, H);
  and and_1 (and_1_out, d_ff_1_qn, d_ff_2_qn, d_ff_3_qn);
  and and_2 (and_2_out, H, and_1_out);
  and and_3 (and_3_out, L, not_1_out);
  and and_4 (and_4_out, R, not_1_out);
  or or_1 (or_1_out, and_13_out, and_2_out);
  or or_2 (or_2_out, and_2_out, and_14_out, and_10_out);
  D_Flip_Flop d_ff_1 (.clk(clock_1_out), .D(or_1_out), .Q(out_7), .Qn(d_ff_1_qn));  // open: preset, en, reset
  D_Flip_Flop d_ff_2 (.clk(clock_1_out), .D(or_2_out), .Q(d_ff_2_q), .Qn(d_ff_2_qn));  // open: preset, en, reset
  D_Flip_Flop d_ff_3 (.clk(clock_1_out), .D(or_3_out), .Q(d_ff_3_q), .Qn(d_ff_3_qn));  // open: preset, en, reset
  or or_3 (or_3_out, and_2_out, and_12_out, and_11_out);
  or or_4 (or_4_out, out_7, d_ff_3_qn);
  xor xor_1 (xor_1_out, d_ff_2_q, d_ff_3_q);
  and and_5 (and_5_out, out_7, d_ff_3_q);
  and and_6 (and_6_out, d_ff_1_qn, d_ff_3_qn);
  and and_7 (and_7_out, out_7, d_ff_2_qn, d_ff_3_qn);
  and and_8 (and_8_out, or_4_out, d_ff_2_qn);
  and and_9 (and_9_out, xor_1_out, d_ff_1_qn);
  and and_10 (and_10_out, and_5_out, and_4_out);
  and and_11 (and_11_out, and_6_out, and_3_out);
  and and_12 (and_12_out, and_7_out, and_4_out);
  and and_13 (and_13_out, and_8_out, and_4_out);
  and and_14 (and_14_out, and_3_out, and_9_out);
  and and_15 (out_4, d_ff_3_q, d_ff_2_q);
  and and_16 (and_16_out, d_ff_2_q, d_ff_1_qn);
  or or_5 (out_5, out_4, and_16_out);
  and and_17 (and_17_out, d_ff_1_qn, d_ff_3_q);
  or or_6 (out_6, out_4, and_16_out, and_17_out);
  and and_18 (and_18_out, d_ff_3_q, out_7);
  or or_7 (out_8, and_18_out, out_9);
  and and_19 (out_9, d_ff_2_q, out_7);

  // Notes on the sheet:
  //   H(A'B'C')
  //   A
  //   B
  //   C
  //   Ak+1
  //   Bk+1
  //   Ck+1
endmodule
